# Fritzing sketch IED Design Challenge Prototype Circuit Complete 04-04-2026 (saved by Fritzing 1.0.6)

parts:
  Auto = SWITCH-MOMENTARY-2 [package=tactile-pth-12mm]
  LCD_1602 = LCD-16X2 [package=lcd-16x2]
  TMC_2209_Stepper_Motor_Driver = TMC2209 [package=THT]
  JACK2 = 2.1mm Barrel Jack with Terminal Block
  Wantai_Stepper_Motor = Stepper Motor - Bipolar
  12V_2A_Power_Supply_from_Screw_Terminal = Power Jack [package=power_jack_smd]
  12V_2A_Power_Supply_from_Screw_Terminal_2 = Power Jack [package=power_jack_smd]
  Joystick = Thumb Joystick
  Manual = SWITCH-MOMENTARY-2 [package=tactile-pth-12mm]
  Home = SWITCH-MOMENTARY-2 [package=tactile-pth-12mm]
  Start/Stop = SWITCH-MOMENTARY-2 [package=tactile-pth-12mm]
  Photoresistor = PHOTOCELL [package=photocell]
  220_uF_capacitor = Capacitor Polarized [package=panasonic_e]
  JACK3 = 2.1mm Barrel Jack with Terminal Block
  S1 = D2F-FL Omron Snap Action Limit Switch with Level
  Micro_limit_switches = D2F-FL Omron Snap Action Limit Switch with Level
  U1 = LM2596 step down module
  Arduino_Protoshield = Adafruit Proto Shield R3 [part_number="Adafruit #2077"]
  LCM1602_IIC = LCM1602 IIC [part_number="LCM1602 IIC" chip_label="LCM1602 IIC" package="DIP (Dual Inline) [THT]"]
  R1 = Resistor [tolerance=±5% power=0.25W resistance=10k package=THT]

nets:
  GND: Auto.1, TMC_2209_Stepper_Motor_Driver.GND, JACK2.NEG, 12V_2A_Power_Supply_from_Screw_Terminal.GND, 12V_2A_Power_Supply_from_Screw_Terminal_2.GND, Joystick.GND, Manual.1, Home.1, Start/Stop.1, 220_uF_capacitor.-, JACK3.NEG, S1.Pin_2, Micro_limit_switches.Pin_2, U1.IN-, U1.OUT-, Arduino_Protoshield.GND, Arduino_Protoshield.1#176, Arduino_Protoshield.P$5#177, Arduino_Protoshield.P$6#178, Arduino_Protoshield.N$16, Arduino_Protoshield.P$5#197, Arduino_Protoshield.P$6#198, Arduino_Protoshield.1#202, Arduino_Protoshield.P$5#203, Arduino_Protoshield.P$6#204, LCM1602_IIC.GND, R1.Pin_1
  N1: Auto.2, Arduino_Protoshield.D12
  VSS: LCD_1602.VSS, LCM1602_IIC.VSS
  VDD: LCD_1602.VDD, LCM1602_IIC.VDD
  N2: LCD_1602.VO, LCM1602_IIC.V0
  N3: LCD_1602.RS, LCM1602_IIC.RS
  N4: LCD_1602.R_W, LCM1602_IIC.RW
  N5: LCD_1602.E, LCM1602_IIC.E
  N6: LCD_1602.DB0, LCM1602_IIC.D0
  N7: LCD_1602.DB1, LCM1602_IIC.D1
  N8: LCD_1602.DB2, LCM1602_IIC.D2
  N9: LCD_1602.DB3, LCM1602_IIC.D3
  N10: LCD_1602.DB4, LCM1602_IIC.D4
  N11: LCD_1602.DB5, LCM1602_IIC.D5
  N12: LCD_1602.DB6, LCM1602_IIC.D6
  N13: LCD_1602.DB7, LCM1602_IIC.D7
  N14: LCD_1602.A, LCM1602_IIC.A
  N15: LCD_1602.K, LCM1602_IIC.K
  5V: TMC_2209_Stepper_Motor_Driver.VIO, Joystick.VCC, Photoresistor.P$2, S1.Pin_3, Micro_limit_switches.Pin_3, Arduino_Protoshield.+5V, Arduino_Protoshield.1#180, Arduino_Protoshield.P$5#181, LCM1602_IIC.VCC
  N16: TMC_2209_Stepper_Motor_Driver.M1B, Wantai_Stepper_Motor.D
  N17: TMC_2209_Stepper_Motor_Driver.M1A, Wantai_Stepper_Motor.B
  N18: TMC_2209_Stepper_Motor_Driver.M2A, Wantai_Stepper_Motor.A
  N19: TMC_2209_Stepper_Motor_Driver.M2B, Wantai_Stepper_Motor.C
  12V: TMC_2209_Stepper_Motor_Driver.VM, JACK2.POS, 12V_2A_Power_Supply_from_Screw_Terminal.PWR, 12V_2A_Power_Supply_from_Screw_Terminal_2.PWR, 220_uF_capacitor.+, U1.IN+, Arduino_Protoshield.1#163, Arduino_Protoshield.P$5#164, Arduino_Protoshield.P$6#165
  N20: TMC_2209_Stepper_Motor_Driver.Dir, Arduino_Protoshield.D5
  N21: TMC_2209_Stepper_Motor_Driver.Step, Arduino_Protoshield.D6
  N22: TMC_2209_Stepper_Motor_Driver.EN, Arduino_Protoshield.D4
  N23: Joystick.SEL, Arduino_Protoshield.A0
  N24: Joystick.HORZ, Arduino_Protoshield.A1
  N25: Joystick.VERT, Arduino_Protoshield.A2
  N26: Manual.2, Arduino_Protoshield.D11
  N27: Home.2, Arduino_Protoshield.D10
  N28: Start/Stop.2, Arduino_Protoshield.D9
  N29: Photoresistor.P$1, Arduino_Protoshield.A3, Arduino_Protoshield.1#126, Arduino_Protoshield.P$5#127, Arduino_Protoshield.P$6#128, R1.Pin_0
  7V: JACK3.POS, U1.OUT+, Arduino_Protoshield.VIN
  N30: S1.Pin_1, Arduino_Protoshield.D8
  N31: Micro_limit_switches.Pin_1, Arduino_Protoshield.D7
  N32: Arduino_Protoshield.A4, LCM1602_IIC.SDA
  N33: Arduino_Protoshield.A5, LCM1602_IIC.SCL

notes:
  Fritzing shows two ratsnest lines here even though the connections are correct because it doesn't know I'm using a DC jack splitter as the power source.

custom parts:
  TMC2209: TMC2209-LA stepper motor controller and driver. Supply voltage 4.75-28V Iphase up to 1.77A rms (2.5A peak)
  D2F-FL Omron Snap Action Limit Switch with Level: Snap action switch with stainless steel lever.
  LM2596 step down module: LM2596 DC-DC step down power supply module 3 A.
  Adafruit Proto Shield R3: This prototyping shield is the best out there (well, we think so, at least), and now is even better with Version R3 - updated for the most compatibility with just about all the Arduinos! It works with UNO, Mega, Leonardo, NG, Diecimila, Duemilanove, and compatible Arduinos. Yun's and Arduino Ethernets have a chunky Ethernet jack that gets in the way of stacking, you can use the stacking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
  LCM1602 IIC: I2C-Module to use a 1602 or 2004 LCD on with the wire.h libory Serial LCD Modul

// code stored in the sketch: Test.ino
// Pin definitions
#define STEP_PIN 2
#define DIR_PIN 3
#define EN_PIN 4

void setup() {
  pinMode(STEP_PIN, OUTPUT);
  pinMode(DIR_PIN, OUTPUT);
  pinMode(EN_PIN, OUTPUT);

  digitalWrite(EN_PIN, LOW); // Enable driver

  Serial.begin(9600);
  Serial.println("Stepper test starting...");
}

void loop() {
  digitalWrite(DIR_PIN, HIGH); // Clockwise
  stepMotor(200); // 200 steps

  delay(500);

  digitalWrite(DIR_PIN, LOW); // Counter-clockwise
  stepMotor(200);

  delay(500);
}

void stepMotor(int steps) {
  for (int i = 0; i < steps; i++) {
    digitalWrite(STEP_PIN, HIGH);
    delayMicroseconds(800);  // adjust speed here
    digitalWrite(STEP_PIN, LOW);
    delayMicroseconds(800);
  }
}
