# Fritzing sketch IED Design Challenge Prototype Circuit Complete 3-21-2026 (saved by Fritzing 1.0.6)

parts:
  Arduino_Uno_R3_will_be_under_the_protoshield = Arduino Uno (Rev3)  # not connected
  Auto = SWITCH-MOMENTARY-2 [package=tactile-pth-12mm]
  LCD_1602 = LCD-16X2 [package=lcd-16x2]
  TMC_2209_Stepper_Motor_Driver = TMC2209 [package=THT]
  JACK2 = 2.1mm Barrel Jack with Terminal Block
  Wantai_Stepper_Motor = Stepper Motor - Bipolar
  Adafruit_Arduino_Protoshield = Adafruit Proto Shield R3 [part_number="Adafruit #2077"]
  Temporary_power_supply = Power Jack [package=power_jack_smd]
  12V_2A_Power_Supply_from_Screw_Terminal = Power Jack [package=power_jack_smd]  # not connected
  Joystick = Thumb Joystick
  Manual = SWITCH-MOMENTARY-2 [package=tactile-pth-12mm]
  Home = SWITCH-MOMENTARY-2 [package=tactile-pth-12mm]
  Start/Stop = SWITCH-MOMENTARY-2 [package=tactile-pth-12mm]
  R1 = PHOTOCELL [package=photocell]
  Micro_limit_switch = YL-99 Limit switch and LED
  Mod2 = YL-99 Limit switch and LED
  LCM1602_IIC = LCM1602 IIC [part_number="LCM1602 IIC" chip_label="LCM1602 IIC" package="DIP (Dual Inline) [THT]"]
  100_uF_capacitor = Capacitor Polarized [package=panasonic_e]

nets:
  N1: Auto.2, Adafruit_Arduino_Protoshield.D13
  VSS: LCD_1602.VSS, LCM1602_IIC.VSS
  VDD: LCD_1602.VDD, LCM1602_IIC.VDD
  N2: LCD_1602.VO, LCM1602_IIC.V0
  N3: LCD_1602.RS, LCM1602_IIC.RS
  N4: LCD_1602.R_W, LCM1602_IIC.RW
  N5: LCD_1602.E, LCM1602_IIC.E
  N6: LCD_1602.DB0, LCM1602_IIC.D0
  N7: LCD_1602.DB1, LCM1602_IIC.D1
  N8: LCD_1602.DB2, LCM1602_IIC.D2
  N9: LCD_1602.DB3, LCM1602_IIC.D3
  N10: LCD_1602.DB4, LCM1602_IIC.D4
  N11: LCD_1602.DB5, LCM1602_IIC.D5
  N12: LCD_1602.DB6, LCM1602_IIC.D6
  N13: LCD_1602.DB7, LCM1602_IIC.D7
  N14: LCD_1602.A, LCM1602_IIC.A
  N15: LCD_1602.K, LCM1602_IIC.K
  GND: TMC_2209_Stepper_Motor_Driver.GND, Adafruit_Arduino_Protoshield.GND, Temporary_power_supply.GND, Joystick.GND, R1.P$2, Micro_limit_switch.GND, Mod2.GND, LCM1602_IIC.GND
  VCC: TMC_2209_Stepper_Motor_Driver.VIO, Adafruit_Arduino_Protoshield.+5V, Joystick.VCC, Micro_limit_switch.VCC, Mod2.VCC, LCM1602_IIC.VCC
  N16: TMC_2209_Stepper_Motor_Driver.M1B, Wantai_Stepper_Motor.D
  N17: TMC_2209_Stepper_Motor_Driver.M1A, Wantai_Stepper_Motor.B
  N18: TMC_2209_Stepper_Motor_Driver.M2A, Wantai_Stepper_Motor.A
  N19: TMC_2209_Stepper_Motor_Driver.M2B, Wantai_Stepper_Motor.C
  N20: TMC_2209_Stepper_Motor_Driver.VM, JACK2.NEG, Adafruit_Arduino_Protoshield.1, Adafruit_Arduino_Protoshield.P$5, Adafruit_Arduino_Protoshield.P$6#174, 100_uF_capacitor.+
  N21: TMC_2209_Stepper_Motor_Driver.Dir, Adafruit_Arduino_Protoshield.D6
  N22: TMC_2209_Stepper_Motor_Driver.Step, Adafruit_Arduino_Protoshield.D7
  N23: TMC_2209_Stepper_Motor_Driver.EN, Adafruit_Arduino_Protoshield.D5
  N24: JACK2.POS, Adafruit_Arduino_Protoshield.N$115, Adafruit_Arduino_Protoshield.P$6#162, 100_uF_capacitor.-
  N25: Adafruit_Arduino_Protoshield.VIN, Temporary_power_supply.PWR
  N26: Adafruit_Arduino_Protoshield.A1, Joystick.SEL
  N27: Adafruit_Arduino_Protoshield.A2, Joystick.HORZ
  N28: Adafruit_Arduino_Protoshield.A3, R1.P$1
  N29: Adafruit_Arduino_Protoshield.A4, LCM1602_IIC.SDA
  N30: Adafruit_Arduino_Protoshield.A5, LCM1602_IIC.SCL
  N31: Adafruit_Arduino_Protoshield.D8, Micro_limit_switch.OUT
  N32: Adafruit_Arduino_Protoshield.D9, Mod2.OUT
  N33: Adafruit_Arduino_Protoshield.D10, Start/Stop.2
  N34: Adafruit_Arduino_Protoshield.D11, Home.2
  N35: Adafruit_Arduino_Protoshield.D12, Manual.2

custom parts:
  TMC2209: TMC2209-LA stepper motor controller and driver. Supply voltage 4.75-28V Iphase up to 1.77A rms (2.5A peak)
  Adafruit Proto Shield R3: This prototyping shield is the best out there (well, we think so, at least), and now is even better with Version R3 - updated for the most compatibility with just about all the Arduinos! It works with UNO, Mega, Leonardo, NG, Diecimila, Duemilanove, and compatible Arduinos. Yun's and Arduino Ethernets have a chunky Ethernet jack that gets in the way of stacking, you can use the stacking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
  LCM1602 IIC: I2C-Module to use a 1602 or 2004 LCD on with the wire.h libory Serial LCD Modul

// code stored in the sketch: Test.ino
// Pin definitions
#define STEP_PIN 2
#define DIR_PIN 3
#define EN_PIN 4

void setup() {
  pinMode(STEP_PIN, OUTPUT);
  pinMode(DIR_PIN, OUTPUT);
  pinMode(EN_PIN, OUTPUT);

  digitalWrite(EN_PIN, LOW); // Enable driver

  Serial.begin(9600);
  Serial.println("Stepper test starting...");
}

void loop() {
  digitalWrite(DIR_PIN, HIGH); // Clockwise
  stepMotor(200); // 200 steps

  delay(500);

  digitalWrite(DIR_PIN, LOW); // Counter-clockwise
  stepMotor(200);

  delay(500);
}

void stepMotor(int steps) {
  for (int i = 0; i < steps; i++) {
    digitalWrite(STEP_PIN, HIGH);
    delayMicroseconds(800);  // adjust speed here
    digitalWrite(STEP_PIN, LOW);
    delayMicroseconds(800);
  }
}
